# Fritzing sketch DFPlayer_and_Nano (saved by Fritzing 0.9.3b)
circuit board: 5.0681cm x 5.57677cm
breadboards: 1

parts:
  Part1 = Arduino Nano (Rev3.0)
  DFRobot_DFPlayer_Mini1 = DFRobot DFPlayer Mini [part_number=DFR0299]
  J1 = Camdenboss CTB0158-4 [part_number=CTB0158-4 package=THT]
  JP1 = Header 3 [package=screwterminal-3.5mm-3_lock.007s]
  J2 = Camdenboss CTB0158-2 [part_number=CTB0158-2 package=THT]
  R1 = Resistor [tolerance=±5% resistance=220 package="1206 [SMD]"]
  LED1 = LED - 5mm [color="Red (633nm)" package="5 mm [THT]"]

nets:
  N1: Part1.GND, DFRobot_DFPlayer_Mini1.GND-1, DFRobot_DFPlayer_Mini1.GND-2, J1.pin2, J1.pin4, JP1.1, LED1.cathode
  N2: Part1.D2, R1.Pin_1
  N3: Part1.D3, DFRobot_DFPlayer_Mini1.TX
  N4: Part1.D7, J2.pin1
  N5: Part1.D8, LED1.anode
  N6: Part1.D9, JP1.2
  5V: Part1.5V, DFRobot_DFPlayer_Mini1.VCC, JP1.3, J2.pin2
  N7: DFRobot_DFPlayer_Mini1.RX, R1.Pin_0
  N8: DFRobot_DFPlayer_Mini1.SPK_1, J1.pin3
  N9: DFRobot_DFPlayer_Mini1.SPK_2, J1.pin1
